// Logisim project MIPS-CPU.circ as structural Verilog
// r6
module RegFile (
  input  [4:0] rs1,
  input  [31:0] busW,
  input  in_3,
  input  [4:0] rs2,
  input  [4:0] rd,
  input  RegWr,
  output [31:0] out_7,
  output [31:0] out_8
);

  wire CLK_DOWN, de0, de1, de2, de3, de4, de5, de6, de7, de8, de9, de10, de11, de12, de13, de14, de15, de16,
       de17, de18, de19, de20, de21, de22, de23, de24, de25, de26, de27, de28, de29, de30, de31;
  wire [31:0] r0, r1, r2, r3, r4, r5, r6, r7, r8, r9, r10, r11, r12, r13, r14, r15, r16, r17, r18, r19, r20,
       r21, r22, r23, r24, r25, r26, r27, r28, r29, r30, r31;

  Register #(.width(32)) register_1 (.D(busW), .en(de0), .Q(r0), .clk(CLK_DOWN));  // open: clr
  Register #(.width(32)) register_2 (.D(busW), .en(de8), .Q(r8), .clk(CLK_DOWN));  // open: clr
  Register #(.width(32)) register_3 (.D(busW), .en(de16), .Q(r16), .clk(CLK_DOWN));  // open: clr
  Register #(.width(32)) register_4 (.D(busW), .en(de24), .Q(r24), .clk(CLK_DOWN));  // open: clr
  Register #(.width(32)) register_5 (.D(busW), .en(de1), .Q(r1), .clk(CLK_DOWN));  // open: clr
  Register #(.width(32)) register_6 (.D(busW), .en(de9), .Q(r9), .clk(CLK_DOWN));  // open: clr
  Register #(.width(32)) register_7 (.D(busW), .en(de17), .Q(r17), .clk(CLK_DOWN));  // open: clr
  Register #(.width(32)) register_8 (.D(busW), .en(de25), .Q(r25), .clk(CLK_DOWN));  // open: clr
  Decoder #(.select(5)) decoder_1 (
    .out0(de0), .out1(de1), .out2(de2), .out3(de3), .out4(de4), .out5(de5), .out6(de6), .out7(de7),
    .out8(de8), .out9(de9), .out10(de10), .out11(de11), .out12(de12), .out13(de13), .out14(de14),
    .out15(de15), .out16(de16), .out17(de17), .out18(de18), .out19(de19), .out20(de20), .out21(de21),
    .out22(de22), .out23(de23), .out24(de24), .out25(de25), .out26(de26), .out27(de27), .out28(de28),
    .out29(de29), .out30(de30), .out31(de31), .sel(rd), .en(RegWr));
  Register #(.width(32)) register_9 (.D(busW), .en(de2), .Q(r2), .clk(CLK_DOWN));  // open: clr
  Register #(.width(32)) register_10 (.D(busW), .en(de10), .Q(r10), .clk(CLK_DOWN));  // open: clr
  Register #(.width(32)) register_11 (.D(busW), .en(de18), .Q(r18), .clk(CLK_DOWN));  // open: clr
  Register #(.width(32)) register_12 (.D(busW), .en(de26), .Q(r26), .clk(CLK_DOWN));  // open: clr
  Register #(.width(32)) register_13 (.D(busW), .en(de3), .Q(r3), .clk(CLK_DOWN));  // open: clr
  Register #(.width(32)) register_14 (.D(busW), .en(de11), .Q(r11), .clk(CLK_DOWN));  // open: clr
  Register #(.width(32)) register_15 (.D(busW), .en(de19), .Q(r19), .clk(CLK_DOWN));  // open: clr
  Register #(.width(32)) register_16 (.D(busW), .en(de27), .Q(r27), .clk(CLK_DOWN));  // open: clr
  Register #(.width(32)) register_17 (.D(busW), .en(de4), .Q(r4), .clk(CLK_DOWN));  // open: clr
  Register #(.width(32)) register_18 (.D(busW), .en(de12), .Q(r12), .clk(CLK_DOWN));  // open: clr
  Register #(.width(32)) register_19 (.D(busW), .en(de20), .Q(r20), .clk(CLK_DOWN));  // open: clr
  Register #(.width(32)) register_20 (.D(busW), .en(de28), .Q(r28), .clk(CLK_DOWN));  // open: clr
  Register #(.width(32)) register_21 (.D(busW), .en(de5), .Q(r5), .clk(CLK_DOWN));  // open: clr
  Register #(.width(32)) register_22 (.D(busW), .en(de13), .Q(r13), .clk(CLK_DOWN));  // open: clr
  Register #(.width(32)) register_23 (.D(busW), .en(de21), .Q(r21), .clk(CLK_DOWN));  // open: clr
  Register #(.width(32)) register_24 (.D(busW), .en(de29), .Q(r29), .clk(CLK_DOWN));  // open: clr
  Multiplexer #(.select(5), .width(32)) multiplexer_1 (
    .in0(r0), .in1(r1), .in2(r2), .in3(r3), .in4(r4), .in5(r5), .in6(r6), .in7(r7), .in8(r8), .in9(r9),
    .in10(r10), .in11(r11), .in12(r12), .in13(r13), .in14(r14), .in15(r15), .in16(r16), .in17(r17),
    .in18(r18), .in19(r19), .in20(r20), .in21(r21), .in22(r22), .in23(r23), .in24(r24), .in25(r25),
    .in26(r26), .in27(r27), .in28(r28), .in29(r29), .in30(r31), .in31(r31), .out(out_7), .sel(rs1));  // open: en
  Multiplexer #(.select(5), .width(32)) multiplexer_2 (
    .in0(r0), .in1(r1), .in2(r2), .in3(r3), .in4(r4), .in5(r5), .in6(r6), .in7(r7), .in8(r8), .in9(r9),
    .in10(r10), .in11(r11), .in12(r12), .in13(r13), .in14(r14), .in15(r15), .in16(r16), .in17(r17),
    .in18(r18), .in19(r19), .in20(r20), .in21(r21), .in22(r22), .in23(r23), .in24(r24), .in25(r25),
    .in26(r26), .in27(r27), .in28(r28), .in29(r29), .in30(r31), .in31(r31), .out(out_8), .sel(rs2));  // open: en
  not not_1 (CLK_DOWN, in_3);
  Register #(.width(32)) register_25 (.D(busW), .en(de6), .Q(r6), .clk(CLK_DOWN));  // open: clr
  Register #(.width(32)) register_26 (.D(busW), .en(de14), .Q(r14), .clk(CLK_DOWN));  // open: clr
  Register #(.width(32)) register_27 (.D(busW), .en(de22), .Q(r22), .clk(CLK_DOWN));  // open: clr
  Register #(.width(32)) register_28 (.D(busW), .en(de30), .Q(r30), .clk(CLK_DOWN));  // open: clr
  Register #(.width(32)) register_29 (.D(busW), .en(de7), .Q(r7), .clk(CLK_DOWN));  // open: clr
  Register #(.width(32)) register_30 (.D(busW), .en(de15), .Q(r15), .clk(CLK_DOWN));  // open: clr
  Register #(.width(32)) register_31 (.D(busW), .en(de23), .Q(r23), .clk(CLK_DOWN));  // open: clr
  Register #(.width(32)) register_32 (.D(busW), .en(de31), .Q(r31), .clk(CLK_DOWN));  // open: clr

  // Other names for the same wires on the sheet: busA[31:0] = out_7; busB[31:0] = out_8
endmodule

module ALU (
  input  [31:0] in_1,
  input  [31:0] in_2,
  input  [2:0] in_3,
  output [31:0] out_4,
  output zero
);

  wire [31:0] adder_1_out, and_1_out, or_1_out, subtractor_1_out;

  Adder #(.width(32)) adder_1 (.a(in_1), .b(in_2), .out(adder_1_out));  // open: cin, cout
  Subtractor #(.width(32)) subtractor_1 (.a(in_1), .b(in_2), .out(subtractor_1_out));  // open: bin, bout
  assign and_1_out = in_1 & in_2;  // AND_Gate and_1, 32 bits wide
  assign or_1_out = in_1 | in_2;  // OR_Gate or_1, 32 bits wide
  nor beq (zero, subtractor_1_out[0], subtractor_1_out[1], subtractor_1_out[2], subtractor_1_out[3], subtractor_1_out[4], subtractor_1_out[5], subtractor_1_out[6], subtractor_1_out[7], subtractor_1_out[8], subtractor_1_out[9], subtractor_1_out[10], subtractor_1_out[11], subtractor_1_out[12], subtractor_1_out[13], subtractor_1_out[14], subtractor_1_out[16], subtractor_1_out[17], subtractor_1_out[18], subtractor_1_out[19], subtractor_1_out[20], subtractor_1_out[21], subtractor_1_out[22], subtractor_1_out[23], subtractor_1_out[24], subtractor_1_out[25], subtractor_1_out[26], subtractor_1_out[27], subtractor_1_out[28], subtractor_1_out[29], subtractor_1_out[30], subtractor_1_out[31]);
  Multiplexer #(.select(3), .width(32)) multiplexer_1 (
    .in0(adder_1_out), .in1(subtractor_1_out), .in2(subtractor_1_out), .in3(and_1_out), .in4(or_1_out),
    .in5({{31{1'b0}}, subtractor_1_out[0]}), .out(out_4), .sel(in_3));  // open: in6, in7, en

  // Other names for the same wires on the sheet: ALUctr[2:0] = in_3; ALUSrc[31:0] = in_2; busA[31:0] = in_1;
  //   result[31:0] = out_4

  // Notes on the sheet:
  //   SUBSTRACOTR
  //   ADDER
  //   AND
  //   sLt
endmodule

module Instruction_Fetch_Unit (
  input  [31:0] in_1,
  input  in_2,
  input  in_3,
  input  in_4
);


  // Other names for the same wires on the sheet: Branch = in_2; Clk = in_4; instruction[31:0] = in_1; Jump = in_3
endmodule

module Controller (
  input  [5:0] in_1,
  input  [5:0] in_2,
  input  [5:0] in_3,
  output out_4,
  output out_5,
  output out_6,
  output out_7,
  output out_8,
  output out_9,
  output out_10,
  output out_11,
  output out_12,
  output out_13,
  output out_14
);

  wire IMMEDIATE_out, not_1_out, not_2_out, not_3_out, not_4_out, not_5_out, not_6_out, ORI_out, R_out,
       SLT_out, SUBI_out;

  not not_1 (not_1_out, in_1[5]);
  not not_2 (not_2_out, in_1[4]);
  not not_3 (not_3_out, in_1[3]);
  not not_4 (not_4_out, in_1[2]);
  not not_5 (not_5_out, in_1[1]);
  not not_6 (not_6_out, in_1[0]);
  and R (R_out, not_1_out, not_2_out, not_3_out, not_4_out, not_5_out, not_6_out);
  or R___SLT (out_4, R_out, SLT_out);
  and LW (out_6, in_1[5], not_2_out, not_3_out, not_4_out, in_1[1], in_1[0]);
  and SW (out_8, in_1[5], not_2_out, in_1[3], not_4_out, in_1[1], in_1[0]);
  or or_1 (out_5, out_6, out_8, IMMEDIATE_out);
  or or_2 (out_7, out_4, out_6, out_6);
  or or_3 (out_11, out_6, out_8, out_9);
  main main_1 ();
  and BEQ (out_9, not_1_out, not_2_out, not_3_out, in_1[2], not_5_out, not_6_out);
  and SUBI (SUBI_out, not_1_out, not_2_out, in_1[3], not_4_out, not_5_out, not_6_out);
  or IMMEDIATE (IMMEDIATE_out, SUBI_out, ORI_out);
  and ORI (ORI_out, not_1_out, not_2_out, in_1[3], in_1[2], not_5_out, in_1[0]);
  and SLT (SLT_out, in_1[5], not_2_out, in_1[3], not_4_out, in_1[1], not_6_out);
  and J (out_10, not_1_out, not_2_out, not_3_out, not_4_out, in_1[1], not_6_out);

  assign in_3 = in_2;

  // Other names for the same wires on the sheet: ALU1 = out_12; ALU2 = out_13; ALU3 = out_14; ALUSrc = out_5;
  //   Branch = out_9; ExtOp = out_11; function[5:0] = in_2; Jump = out_10; MemtoReg = out_6; MemWrite = out_8;
  //   opcode[5:0] = in_1; RegDst = out_4; RegWrite = out_7

  // Notes on the sheet:
  //   SW
  //   beq
  //   R+SLT
  //   LW
  //   j
  //   J
  //   imm
endmodule

module Extender (
  input  [15:0] imm16,
  input  ExtOp,
  output [31:0] out_3
);

  wire and_1_out;

  Multiplexer #(.width(32)) multiplexer_1 (
    .in0({{16{1'b0}}, imm16}), .in1({{16{1'b1}}, imm16}), .out(out_3), .sel(and_1_out));  // open: en
  and and_1 (and_1_out, imm16[15], ExtOp);

  // Other names for the same wires on the sheet: imm32[31:0] = out_3
endmodule

module Data_Memory (
  input  [31:0] in_1,
  input  [7:0] in_2,
  input  in_3,
  input  in_4,
  input  reset,
  output [31:0] out_6
);

  wire not_1_out;

  not not_1 (not_1_out, in_4);
  RAM #(.dataWidth(32), .bus("separate")) ram_1 (
    .addr(in_2), .din(in_1), .data(out_6), .str(in_3), .sel(1'b1), .clk(not_1_out), .ld(1'b1), .clr(reset));

  // Other names for the same wires on the sheet: addr[7:0] = in_2; Clk = in_4; data_in[31:0] = in_1;
  //   data_out[31:0] = out_6; MemWrite = in_3
endmodule
