// Logisim project mipscpu.circ as structural Verilog: 9 circuits, main circuit main
module main (
  input  in_1
);

  wire ALUSrc, Branch, CLOCK, ExtOp, Jump, MemtoReg, MemWrite, RegDst, RegWrite, Zero;
  wire [2:0] ALUop, controller_alu_1_p10;
  wire [4:0] multiplexer_2_out;
  wire [5:0] \function , opcode;
  wire [15:6] imm16;
  wire [25:16] imm26;
  wire [31:0] busA, busB, busW, data_memory_1_out_6, Imm32, imm32_t, npc_1_out_8, Result;

  Clock clock_1 (.out(CLOCK));
  RegFile regfile_1 (
    .rs1(imm26[25:21]), .out_8(busA), .out_9(busB), .busW(busW), .in_3(CLOCK), .rs2(imm26[20:16]),
    .RegWr(RegWrite), .reset(in_1), .rd(multiplexer_2_out));
  Extender extender_1 (.imm16({imm16, \function }), .out_3(imm32_t), .ExtOp(ExtOp));
  NPC npc_1 (
    .in_1(imm32_t), .in_2(Branch), .in_3(CLOCK), .out_8(npc_1_out_8), .reset(in_1),
    .Imm2({imm26, imm16, \function }), .Zero(Zero), .Jump(Jump));
  // Probe on Imm32
  Multiplexer #(.width(32)) multiplexer_1 (.in0(busB), .in1(imm32_t), .out(Imm32), .sel(ALUSrc));  // open: en
  // Probe on imm32_t
  Multiplexer #(.width(5)) multiplexer_2 (
    .in0(imm26[20:16]), .in1(imm16[15:11]), .out(multiplexer_2_out), .sel(RegDst));  // open: en
  // Controller_ALU controller_alu_1: pin names not known; wires that end beside it: \function [3], \function [2], \function [1], \function [0], ALUop[2], ALUop[1], ALUop[0], controller_alu_1_p10[2], controller_alu_1_p10[1], controller_alu_1_p10[0]
  ALU alu_1 (.in_1(busA), .in_2(Imm32), ._000_and(controller_alu_1_p10), .out_4(Result), .zero(Zero));
  // Probe on Result
  ROM #(.addrWidth(24), .dataWidth(32)) rom_1 (
    .addr(npc_1_out_8[25:2]), .data({opcode, imm26, imm16, \function }), .sel(1'b1));
  Controller controller_1 (
    .op5(opcode[5]), .op4(opcode[4]), .RegDst(RegDst), .op3(opcode[3]), .op2(opcode[2]), .op1(opcode[1]),
    .op0(opcode[0]), .ALUSrc(ALUSrc), .MemtoReg(MemtoReg), .RegWrite(RegWrite), .MemWrite(MemWrite),
    .Branch(Branch), .Jump(Jump), .ExtOp(ExtOp), .ALU1(ALUop[0]), .ALU2(ALUop[1]), .ALU3(ALUop[2]));
  Data_Memory data_memory_1 (
    .in_1(busB), .in_2(Result[9:2]), .in_3(MemWrite), .in_4(CLOCK), .out_6(data_memory_1_out_6), .reset(in_1));
  // Probe on busW
  Multiplexer #(.width(32)) multiplexer_3 (
    .in0(Result), .in1(data_memory_1_out_6), .out(busW), .sel(MemtoReg));  // open: en

  // Other names for the same wires on the sheet: imm16[5:0] = \function ; imm26[15:0] = {imm16, \function };
  //   rd[4:0] = imm16[15:11]; rs2[4:0] = imm26[20:16]; rs1[4:0] = imm26[25:21]; RESET = in_1

  // Notes on the sheet:
  //   contents of rom_1 (hex, n*v repeats v):
  //   34010001 211020 221824 222025 64282a c53022 ac060004 8c070004 21290012 10c70001 34010001 8000000
endmodule

// r6
module RegFile (
  input  [4:0] rs1,
  input  [31:0] busW,
  input  in_3,
  input  [4:0] rs2,
  input  [4:0] rd,
  input  reset,
  input  RegWr,
  output [31:0] out_8,
  output [31:0] out_9
);

  wire CLK_DOWN, de0, de1, de2, de3, de4, de5, de6, de7, de8, de9, de10, de11, de12, de13, de14, de15, de16,
       de17, de18, de19, de20, de21, de22, de23, de24, de25, de26, de27, de28, de29, de30, de31,
       decoder_1_out0, decoder_1_out1, decoder_1_out2, decoder_1_out3, decoder_1_out4, decoder_1_out5,
       decoder_1_out6, decoder_1_out7, decoder_1_out8, decoder_1_out9, decoder_1_out10, decoder_1_out11,
       decoder_1_out12, decoder_1_out13, decoder_1_out14, decoder_1_out15, decoder_1_out16, decoder_1_out17,
       decoder_1_out18, decoder_1_out19, decoder_1_out20, decoder_1_out21, decoder_1_out22, decoder_1_out23,
       decoder_1_out24, decoder_1_out25, decoder_1_out26, decoder_1_out27, decoder_1_out28, decoder_1_out29,
       decoder_1_out30, decoder_1_out31;
  wire [31:0] r0, r1, r2, r3, r4, r5, r6, r7, r8, r9, r10, r11, r12, r13, r14, r15, r16, r17, r18, r19, r20,
       r21, r22, r23, r24, r25, r26, r27, r28, r29, r30, r31;

  // Probe on rd
  Register #(.width(32)) register_1 (.D(busW), .en(de0), .Q(r0), .clk(CLK_DOWN), .clr(reset));
  // Probe on r1
  Register #(.width(32)) register_2 (.D(busW), .en(de8), .Q(r8), .clk(CLK_DOWN), .clr(reset));
  Register #(.width(32)) register_3 (.D(busW), .en(de16), .Q(r16), .clk(CLK_DOWN), .clr(reset));
  Register #(.width(32)) register_4 (.D(busW), .en(de24), .Q(r24), .clk(CLK_DOWN), .clr(reset));
  Register #(.width(32)) register_5 (.D(busW), .en(de1), .Q(r1), .clk(CLK_DOWN), .clr(reset));
  Register #(.width(32)) register_6 (.D(busW), .en(de9), .Q(r9), .clk(CLK_DOWN), .clr(reset));
  Register #(.width(32)) register_7 (.D(busW), .en(de25), .Q(r25), .clk(CLK_DOWN), .clr(reset));
  Decoder #(.select(5)) decoder_1 (
    .out0(decoder_1_out0), .out1(decoder_1_out1), .out2(decoder_1_out2), .out3(decoder_1_out3),
    .out4(decoder_1_out4), .out5(decoder_1_out5), .out6(decoder_1_out6), .out7(decoder_1_out7),
    .out8(decoder_1_out8), .out9(decoder_1_out9), .out10(decoder_1_out10), .out11(decoder_1_out11),
    .out12(decoder_1_out12), .out13(decoder_1_out13), .out14(decoder_1_out14), .out15(decoder_1_out15),
    .out16(decoder_1_out16), .out17(decoder_1_out17), .out18(decoder_1_out18), .out19(decoder_1_out19),
    .out20(decoder_1_out20), .out21(decoder_1_out21), .out22(decoder_1_out22), .out23(decoder_1_out23),
    .out24(decoder_1_out24), .out25(decoder_1_out25), .out26(decoder_1_out26), .out27(decoder_1_out27),
    .out28(decoder_1_out28), .out29(decoder_1_out29), .out30(decoder_1_out30), .out31(decoder_1_out31),
    .sel(rd), .en(1'b1));
  // Probe on nothing
  // Probe on r9
  Register #(.width(32)) register_8 (.D(busW), .en(de17), .Q(r17), .clk(CLK_DOWN), .clr(reset));
  and and_1 (de0, RegWr, decoder_1_out0);
  Register #(.width(32)) register_9 (.D(busW), .en(de2), .Q(r2), .clk(CLK_DOWN), .clr(reset));
  // Probe on r2
  Register #(.width(32)) register_10 (.D(busW), .en(de10), .Q(r10), .clk(CLK_DOWN), .clr(reset));
  Register #(.width(32)) register_11 (.D(busW), .en(de18), .Q(r18), .clk(CLK_DOWN), .clr(reset));
  Register #(.width(32)) register_12 (.D(busW), .en(de26), .Q(r26), .clk(CLK_DOWN), .clr(reset));
  and and_2 (de1, RegWr, decoder_1_out1);
  and and_3 (de2, RegWr, decoder_1_out2);
  // Probe on r3
  and and_4 (de4, RegWr, decoder_1_out4);
  and and_5 (de3, RegWr, decoder_1_out3);
  Register #(.width(32)) register_13 (.D(busW), .en(de3), .Q(r3), .clk(CLK_DOWN), .clr(reset));
  Register #(.width(32)) register_14 (.D(busW), .en(de11), .Q(r11), .clk(CLK_DOWN), .clr(reset));
  Register #(.width(32)) register_15 (.D(busW), .en(de19), .Q(r19), .clk(CLK_DOWN), .clr(reset));
  Register #(.width(32)) register_16 (.D(busW), .en(de27), .Q(r27), .clk(CLK_DOWN), .clr(reset));
  and and_6 (de6, RegWr, decoder_1_out6);
  and and_7 (de5, RegWr, decoder_1_out5);
  Register #(.width(32)) register_17 (.D(busW), .en(de4), .Q(r4), .clk(CLK_DOWN), .clr(reset));
  // Probe on r4
  Register #(.width(32)) register_18 (.D(busW), .en(de28), .Q(r28), .clk(CLK_DOWN), .clr(reset));
  and and_8 (de8, RegWr, decoder_1_out8);
  and and_9 (de7, RegWr, decoder_1_out7);
  Register #(.width(32)) register_19 (.D(busW), .en(de12), .Q(r12), .clk(CLK_DOWN), .clr(reset));
  Register #(.width(32)) register_20 (.D(busW), .en(de20), .Q(r20), .clk(CLK_DOWN), .clr(reset));
  and and_10 (de10, RegWr, decoder_1_out10);
  and and_11 (de9, RegWr, decoder_1_out9);
  Register #(.width(32)) register_21 (.D(busW), .en(de5), .Q(r5), .clk(CLK_DOWN), .clr(reset));
  // Probe on r5
  Register #(.width(32)) register_22 (.D(busW), .en(de13), .Q(r13), .clk(CLK_DOWN), .clr(reset));
  Register #(.width(32)) register_23 (.D(busW), .en(de29), .Q(r29), .clk(CLK_DOWN), .clr(reset));
  and and_12 (de11, RegWr, decoder_1_out11);
  and and_13 (de12, RegWr, decoder_1_out12);
  Multiplexer #(.select(5), .width(32)) multiplexer_1 (
    .in0(r0), .in1(r1), .in2(r2), .in3(r3), .in4(r4), .in5(r5), .in6(r6), .in7(r7), .in8(r8), .in9(r9),
    .in10(r10), .in11(r11), .in12(r12), .in13(r13), .in14(r14), .in15(r15), .in16(r16), .in17(r17),
    .in18(r18), .in19(r19), .in20(r20), .in21(r21), .in22(r22), .in23(r23), .in24(r24), .in25(r25),
    .in26(r26), .in27(r27), .in28(r28), .in29(r29), .in30(r31), .in31(r31), .out(out_8), .sel(rs1));  // open: en
  Multiplexer #(.select(5), .width(32)) multiplexer_2 (
    .in0(r0), .in1(r1), .in2(r2), .in3(r3), .in4(r4), .in5(r5), .in6(r6), .in7(r7), .in8(r8), .in9(r9),
    .in10(r10), .in11(r11), .in12(r12), .in13(r13), .in14(r14), .in15(r15), .in16(r16), .in17(r17),
    .in18(r18), .in19(r19), .in20(r20), .in21(r21), .in22(r22), .in23(r23), .in24(r24), .in25(r25),
    .in26(r26), .in27(r27), .in28(r28), .in29(r29), .in30(r31), .in31(r31), .out(out_9), .sel(rs2));  // open: en
  Register #(.width(32)) register_24 (.D(busW), .en(de21), .Q(r21), .clk(CLK_DOWN), .clr(reset));
  and and_14 (de13, RegWr, decoder_1_out13);
  and and_15 (de14, RegWr, decoder_1_out14);
  Register #(.width(32)) register_25 (.D(busW), .en(de6), .Q(r6), .clk(CLK_DOWN), .clr(reset));
  // Probe on r6
  Register #(.width(32)) register_26 (.D(busW), .en(de14), .Q(r14), .clk(CLK_DOWN), .clr(reset));
  Register #(.width(32)) register_27 (.D(busW), .en(de22), .Q(r22), .clk(CLK_DOWN), .clr(reset));
  Register #(.width(32)) register_28 (.D(busW), .en(de30), .Q(r30), .clk(CLK_DOWN), .clr(reset));
  and and_16 (de15, RegWr, decoder_1_out15);
  and and_17 (de16, RegWr, decoder_1_out16);
  // Probe on r7
  and and_18 (de17, RegWr, decoder_1_out17);
  and and_19 (de18, RegWr, decoder_1_out18);
  Register #(.width(32)) register_29 (.D(busW), .en(de7), .Q(r7), .clk(CLK_DOWN), .clr(reset));
  Register #(.width(32)) register_30 (.D(busW), .en(de15), .Q(r15), .clk(CLK_DOWN), .clr(reset));
  Register #(.width(32)) register_31 (.D(busW), .en(de23), .Q(r23), .clk(CLK_DOWN), .clr(reset));
  Register #(.width(32)) register_32 (.D(busW), .en(de31), .Q(r31), .clk(CLK_DOWN), .clr(reset));
  and and_20 (de20, RegWr, decoder_1_out20);
  and and_21 (de19, RegWr, decoder_1_out19);
  and and_22 (de21, RegWr, decoder_1_out21);
  and and_23 (de22, RegWr, decoder_1_out22);
  and and_24 (de23, RegWr, decoder_1_out23);
  and and_25 (de24, RegWr, decoder_1_out24);
  and and_26 (de25, RegWr, decoder_1_out25);
  and and_27 (de26, RegWr, decoder_1_out26);
  and and_28 (de28, RegWr, decoder_1_out28);
  and and_29 (de27, RegWr, decoder_1_out27);
  and and_30 (de29, RegWr, decoder_1_out29);
  and and_31 (de30, RegWr, decoder_1_out30);
  and and_32 (de31, RegWr, decoder_1_out31);
  not not_1 (CLK_DOWN, in_3);

  // Other names for the same wires on the sheet: busA[31:0] = out_8; busB[31:0] = out_9
endmodule

module ALU (
  input  [31:0] in_1,
  input  [31:0] in_2,
  input  [2:0] _000_and,
  output [31:0] out_4,
  output zero
);

  wire [31:0] adder_1_out, and_1_out, or_1_out, subtractor_1_out;

  Adder #(.width(32)) adder_1 (.a(in_1), .b(in_2), .out(adder_1_out));  // open: cin, cout
  Subtractor #(.width(32)) subtractor_1 (.a(in_1), .b(in_2), .out(subtractor_1_out));  // open: bin, bout
  assign and_1_out = in_1 & in_2;  // AND_Gate and_1, 32 bits wide
  assign or_1_out = in_1 | in_2;  // OR_Gate or_1, 32 bits wide
  nor beq (zero, subtractor_1_out[0], subtractor_1_out[1], subtractor_1_out[2], subtractor_1_out[3], subtractor_1_out[4], subtractor_1_out[5], subtractor_1_out[6], subtractor_1_out[7], subtractor_1_out[8], subtractor_1_out[9], subtractor_1_out[10], subtractor_1_out[11], subtractor_1_out[12], subtractor_1_out[13], subtractor_1_out[14], subtractor_1_out[16], subtractor_1_out[17], subtractor_1_out[18], subtractor_1_out[19], subtractor_1_out[20], subtractor_1_out[21], subtractor_1_out[22], subtractor_1_out[23], subtractor_1_out[24], subtractor_1_out[25], subtractor_1_out[26], subtractor_1_out[27], subtractor_1_out[28], subtractor_1_out[29], subtractor_1_out[30], subtractor_1_out[31]);
  Multiplexer #(.select(3), .width(32)) multiplexer_1 (
    .in0(and_1_out), .in1(or_1_out), .in2(adder_1_out), .in6(subtractor_1_out),
    .in7({{31{1'b0}}, subtractor_1_out[31]}), .out(out_4), .sel(_000_and));  // open: in3, in4, in5, en

  // Other names for the same wires on the sheet: ALUctr[2:0] = _000_and; ALUSrc[31:0] = in_2; busA[31:0] = in_1;
  //   result[31:0] = out_4

  // Notes on the sheet:
  //   SUBSTRACOTR
  //   001 or
  //   011 NA
  //   100 NA
  //   101 NA
  //   110 sub
  //   ADDER
  //   AND
  //   010 add
  //   111 sub_slt
  //   sLt
endmodule

module Controller (
  input  op5,
  input  op4,
  input  op3,
  input  op2,
  input  op1,
  input  op0,
  output RegDst,
  output ALUSrc,
  output MemtoReg,
  output RegWrite,
  output MemWrite,
  output Branch,
  output Jump,
  output ExtOp,
  output ALU1,
  output ALU2,
  output ALU3
);

  wire and_2_out, and_3_out, and_4_out, and_5_out, and_7_out, and_8_out, and_9_out, and_10_out, and_14_out,
       and_15_out, and_16_out, and_17_out, and_18_out, and_19_out, and_20_out, not_1_out, not_2_out,
       not_3_out, not_4_out, not_5_out, not_6_out, not_7_out, not_8_out, not_9_out, not_10_out, not_11_out,
       not_12_out, not_13_out, not_14_out, not_15_out, not_16_out, not_17_out, not_18_out, not_19_out,
       not_20_out, not_21_out, not_22_out, not_23_out, not_24_out, not_25_out, not_26_out, not_27_out,
       not_28_out, not_29_out, not_30_out, not_31_out, not_32_out, not_33_out, not_34_out, not_35_out,
       not_36_out, not_37_out, not_38_out, not_39_out, not_40_out, not_41_out, not_42_out, not_43_out,
       not_44_out, not_45_out, not_46_out, not_47_out, not_48_out, not_49_out, not_50_out, not_51_out,
       not_52_out, not_53_out, not_54_out, not_55_out, not_56_out, not_57_out, not_58_out, not_59_out,
       not_60_out, not_61_out, not_62_out, not_63_out, not_64_out, not_65_out, not_66_out, not_67_out,
       not_68_out, not_69_out, not_70_out, not_71_out, not_72_out, not_73_out, not_74_out, not_75_out,
       not_76_out, not_77_out, not_78_out, not_79_out, not_80_out, not_81_out, not_82_out, not_83_out,
       not_84_out, not_85_out;

  not not_1 (not_1_out, op5);
  not not_2 (not_2_out, op4);
  not not_3 (not_3_out, op3);
  not not_4 (not_4_out, op2);
  not not_5 (not_5_out, op1);
  not not_6 (not_6_out, op0);
  not not_7 (not_7_out, op5);
  not not_8 (not_8_out, op4);
  not not_9 (not_9_out, op1);
  not not_10 (not_10_out, op4);
  not not_11 (not_11_out, op3);
  not not_12 (not_12_out, op2);
  not not_13 (not_13_out, op4);
  not not_14 (not_14_out, op2);
  not not_15 (not_15_out, op5);
  not not_16 (not_16_out, op4);
  not not_17 (not_17_out, op2);
  not not_18 (not_18_out, op1);
  not not_19 (not_19_out, op0);
  not not_20 (not_20_out, op4);
  not not_21 (not_21_out, op3);
  not not_22 (not_22_out, op2);
  not not_23 (not_23_out, op4);
  not not_24 (not_24_out, op3);
  not not_25 (not_25_out, op2);
  not not_26 (not_26_out, op5);
  not not_27 (not_27_out, op4);
  not not_28 (not_28_out, op3);
  not not_29 (not_29_out, op2);
  not not_30 (not_30_out, op1);
  not not_31 (not_31_out, op0);
  not not_32 (not_32_out, op5);
  not not_33 (not_33_out, op4);
  not not_34 (not_34_out, op1);
  not not_35 (not_35_out, op5);
  not not_36 (not_36_out, op4);
  not not_37 (not_37_out, op2);
  not not_38 (not_38_out, op1);
  not not_39 (not_39_out, op0);
  not not_40 (not_40_out, op4);
  not not_41 (not_41_out, op2);
  not not_42 (not_42_out, op5);
  not not_43 (not_43_out, op4);
  not not_44 (not_44_out, op3);
  not not_45 (not_45_out, op1);
  not not_46 (not_46_out, op0);
  not not_47 (not_47_out, op5);
  not not_48 (not_48_out, op4);
  not not_49 (not_49_out, op3);
  not not_50 (not_50_out, op2);
  not not_51 (not_51_out, op0);
  not not_52 (not_52_out, op4);
  not not_53 (not_53_out, op3);
  not not_54 (not_54_out, op2);
  not not_55 (not_55_out, op4);
  not not_56 (not_56_out, op2);
  not not_57 (not_57_out, op5);
  not not_58 (not_58_out, op4);
  not not_59 (not_59_out, op3);
  not not_60 (not_60_out, op1);
  not not_61 (not_61_out, op0);
  not not_62 (not_62_out, op5);
  not not_63 (not_63_out, op4);
  not not_64 (not_64_out, op3);
  not not_65 (not_65_out, op1);
  not not_66 (not_66_out, op0);
  not not_67 (not_67_out, op5);
  not not_68 (not_68_out, op4);
  not not_69 (not_69_out, op2);
  not not_70 (not_70_out, op1);
  not not_71 (not_71_out, op0);
  not not_72 (not_72_out, op5);
  not not_73 (not_73_out, op4);
  not not_74 (not_74_out, op1);
  not not_75 (not_75_out, op5);
  not not_76 (not_76_out, op4);
  not not_77 (not_77_out, op2);
  not not_78 (not_78_out, op1);
  not not_79 (not_79_out, op0);
  not not_80 (not_80_out, op5);
  not not_81 (not_81_out, op4);
  not not_82 (not_82_out, op3);
  not not_83 (not_83_out, op2);
  not not_84 (not_84_out, op1);
  not not_85 (not_85_out, op0);
  and and_1 (RegDst, not_1_out, not_2_out, not_3_out, not_4_out, not_5_out, not_6_out);
  and and_2 (and_2_out, not_7_out, not_8_out, op3, op2, not_9_out, op0);
  and and_3 (and_3_out, op5, not_10_out, not_11_out, not_12_out, op1, op0);
  and and_4 (and_4_out, op5, not_13_out, op3, not_14_out, op1, op0);
  and and_5 (and_5_out, not_15_out, not_16_out, op3, not_17_out, not_18_out, not_19_out);
  and and_6 (MemtoReg, op5, not_20_out, not_21_out, not_22_out, op1, op0);
  and and_7 (and_7_out, op5, not_23_out, not_24_out, not_25_out, op1, op0);
  and and_8 (and_8_out, not_26_out, not_27_out, not_28_out, not_29_out, not_30_out, not_31_out);
  and and_9 (and_9_out, not_32_out, not_33_out, op3, op2, not_34_out, op0);
  and and_10 (and_10_out, not_35_out, not_36_out, op3, not_37_out, not_38_out, not_39_out);
  and and_11 (MemWrite, op5, not_40_out, op3, not_41_out, op1, op0);
  and and_12 (Branch, not_42_out, not_43_out, not_44_out, op2, not_45_out, not_46_out);
  and and_13 (Jump, not_47_out, not_48_out, not_49_out, not_50_out, op1, not_51_out);
  and and_14 (and_14_out, op5, not_52_out, not_53_out, not_54_out, op1, op0);
  and and_15 (and_15_out, op5, not_55_out, op3, not_56_out, op1, op0);
  and and_16 (and_16_out, not_57_out, not_58_out, not_59_out, op2, not_60_out, not_61_out);
  and and_17 (and_17_out, not_62_out, not_63_out, not_64_out, op2, not_65_out, not_66_out);
  and and_18 (and_18_out, not_67_out, not_68_out, op3, not_69_out, not_70_out, not_71_out);
  and and_19 (and_19_out, not_72_out, not_73_out, op3, op2, not_74_out, op0);
  and and_20 (and_20_out, not_75_out, not_76_out, op3, not_77_out, not_78_out, not_79_out);
  and and_21 (ALU3, not_80_out, not_81_out, not_82_out, not_83_out, not_84_out, not_85_out);
  or or_1 (ALUSrc, and_2_out, and_3_out, and_4_out, and_5_out);
  or or_2 (RegWrite, and_7_out, and_8_out, and_9_out, and_10_out);
  or or_3 (ExtOp, and_14_out, and_15_out, and_16_out);
  or or_4 (ALU1, and_17_out, and_18_out);
  or or_5 (ALU2, and_19_out, and_20_out);
endmodule

module Extender (
  input  [15:0] imm16,
  input  ExtOp,
  output [31:0] out_3
);

  wire and_1_out;

  Multiplexer #(.width(32)) multiplexer_1 (
    .in0({{16{1'b0}}, imm16}), .in1({{16{1'b1}}, imm16}), .out(out_3), .sel(and_1_out));  // open: en
  and and_1 (and_1_out, imm16[15], ExtOp);
  // Probe on out_3

  // Other names for the same wires on the sheet: imm32[31:0] = out_3
endmodule

module Data_Memory (
  input  [31:0] in_1,
  input  [7:0] in_2,
  input  in_3,
  input  in_4,
  input  reset,
  output [31:0] out_6
);

  wire not_1_out;

  not not_1 (not_1_out, in_4);
  RAM #(.dataWidth(32), .bus("separate")) ram_1 (
    .addr(in_2), .din(in_1), .data(out_6), .str(in_3), .sel(1'b1), .clk(not_1_out), .ld(1'b1), .clr(reset));

  // Other names for the same wires on the sheet: addr[7:0] = in_2; Clk = in_4; data_in[31:0] = in_1;
  //   data_out[31:0] = out_6; MemWrite = in_3
endmodule

module Controller_ALU (
  input  ALU3,
  input  ALU2,
  input  ALU1,
  input  func3,
  input  func2,
  input  func1,
  input  func0,
  output ALUctr3,
  output ALUctr2,
  output ALUctr1
);

  wire and_1_out, and_2_out, and_3_out, and_4_out, and_5_out, and_6_out, and_7_out, and_8_out, and_9_out,
       and_10_out, and_11_out, and_12_out, not_1_out, not_2_out, not_3_out, not_4_out, not_5_out, not_6_out,
       not_7_out, not_8_out, not_9_out, not_10_out, not_11_out, not_12_out, not_13_out, not_14_out,
       not_15_out, not_16_out, not_17_out, not_18_out, not_19_out, not_20_out, not_21_out, not_22_out,
       not_23_out, not_24_out, not_25_out, not_26_out, not_27_out, not_28_out;

  not not_1 (not_1_out, ALU3);
  not not_2 (not_2_out, ALU2);
  not not_3 (not_3_out, func3);
  not not_4 (not_4_out, func2);
  not not_5 (not_5_out, func0);
  not not_6 (not_6_out, func2);
  not not_7 (not_7_out, func0);
  not not_8 (not_8_out, ALU3);
  not not_9 (not_9_out, ALU2);
  not not_10 (not_10_out, ALU1);
  not not_11 (not_11_out, ALU3);
  not not_12 (not_12_out, ALU2);
  not not_13 (not_13_out, func3);
  not not_14 (not_14_out, func2);
  not not_15 (not_15_out, func1);
  not not_16 (not_16_out, func0);
  not not_17 (not_17_out, func3);
  not not_18 (not_18_out, func2);
  not not_19 (not_19_out, func0);
  not not_20 (not_20_out, func2);
  not not_21 (not_21_out, func0);
  not not_22 (not_22_out, ALU3);
  not not_23 (not_23_out, ALU3);
  not not_24 (not_24_out, ALU1);
  not not_25 (not_25_out, func3);
  not not_26 (not_26_out, func1);
  not not_27 (not_27_out, func2);
  not not_28 (not_28_out, func0);
  and and_1 (and_1_out, not_1_out, not_2_out, ALU1);
  and and_2 (and_2_out, ALU3, not_3_out, not_4_out, func1, not_5_out);
  and and_3 (and_3_out, ALU3, func3, not_6_out, func1, not_7_out);
  and and_4 (and_4_out, not_8_out, not_9_out, not_10_out);
  and and_5 (and_5_out, not_11_out, not_12_out, ALU1);
  and and_6 (and_6_out, ALU3, not_13_out, not_14_out, not_15_out, not_16_out);
  and and_7 (and_7_out, ALU3, not_17_out, not_18_out, func1, not_19_out);
  and and_8 (and_8_out, ALU3, func3, not_20_out, func1, not_21_out);
  and and_9 (and_9_out, not_22_out, ALU2, ALU1);
  and and_10 (and_10_out, not_23_out, ALU2, not_24_out);
  and and_11 (and_11_out, ALU3, not_25_out, func2, not_26_out, func0);
  and and_12 (and_12_out, ALU3, func3, not_27_out, func1, not_28_out);
  or or_1 (ALUctr3, and_1_out, and_2_out, and_3_out);
  or or_2 (ALUctr2, and_4_out, and_5_out, and_6_out, and_7_out, and_8_out, and_9_out);
  or or_3 (ALUctr1, and_10_out, and_11_out, and_12_out);
endmodule

module NPC (
  input  [31:0] in_1,
  input  in_2,
  input  in_3,
  input  reset,
  input  [25:0] Imm2,
  input  Zero,
  input  Jump,
  output [31:0] out_8
);

  wire and_1_out, not_1_out;
  wire [27:0] adder_1_out;
  wire [31:0] adder_2_out, multiplexer_2_out, t1;
  wire [31:28] t2;

  not not_1 (not_1_out, in_3);
  // Probe on in_1
  Register #(.width(32)) register_1 (.D(multiplexer_2_out), .en(1'b1), .Q(out_8), .clk(not_1_out), .clr(reset));
  // Probe on multiplexer_2_out
  // Probe on out_8
  Adder #(.width(32)) adder_1 (.a(out_8), .b(32'h4), .out({t2, adder_1_out}), .cin(1'b0));  // open: cout
  // Probe on {t2, adder_1_out}
  // Probe on {in_1[29:0], 2'b00}
  // Probe on multiplexer_2_out
  // Probe on Jump
  // Probe on adder_2_out
  Adder #(.width(32)) adder_2 (
    .a({t2, adder_1_out}), .b({in_1[29:0], 2'b00}), .out(adder_2_out), .cin(1'b0));  // open: cout
  Multiplexer #(.width(32)) multiplexer_1 (
    .in0({t2, adder_1_out}), .in1(adder_2_out), .out(t1), .sel(and_1_out));  // open: en
  // Probe on t1
  // Probe on and_1_out
  and and_1 (and_1_out, Zero, in_2);
  Multiplexer #(.width(32)) multiplexer_2 (
    .in0(t1), .in1({t2, Imm2, 2'b00}), .out(multiplexer_2_out), .sel(Jump));  // open: en
  // Probe on {t2, Imm2, 2'b00}
  // Probe on t1

  // Other names for the same wires on the sheet: Imm32[31:0] = in_1; Branch = in_2; Clk = in_3; PC[31:0] = out_8;
  //   Imm26[25:0] = Imm2; t2[27:2] = Imm2
endmodule

module draft (
  input  [7:0] in_1,
  input  in_2,
  output [7:0] out_3
);

  wire clock_1_out;

  Clock clock_1 (.out(clock_1_out));
  Register register_1 (.D(in_1), .en(1'b1), .Q(out_3), .clk(clock_1_out), .clr(in_2));
endmodule
